# Fritzing sketch TermostatProgramı (saved by Fritzing 0.9.3b)
breadboards: 1

parts:
  U1 = NodeMCU V3.0
  DHT1 = DHT11 Humitidy and Temperature Sensor (3 pins)
  Parça1 = Adafruit DS1307 RTC Breakout [part_number="Adafruit #264"]
  U2 = 2-Channel 5v Relay Shield [package=relay-2ch5v10a]
  o1 = Module display OLED I2C 128x64 SSD1306 [package=THT]

nets:
  N1: U1.D1, Parça1.SCL, o1.SCL
  N2: U1.D2, Parça1.SDA, o1.SDA
  N3: U1.D3, U2.IN1
  3V3: U1.3V3, DHT1.VDD
  N4: U1.GND#6, U1.GND#13, U1.GND#16, U1.GND#33
  N5: U1.D5, DHT1.DATA
  VCC: U1.VU, Parça1.VCC, U2.VCC, U2.IN2
  GND: U1.GND#41, Parça1.GND, U2.GND

notes:
  DHT11 = > D5
  DS1307 RTC SDA => D2
  SCL => D1
  5V => VU
  OLED I2C SDA => D2
  SCL => D1
  Röle In1 = > D3
  VCC 5V = > VU
  NodeMCU LoLin V3
  Blynk App

custom parts:
  NodeMCU V3.0: ESP8266 based NodeMCU
  DHT11 Humitidy and Temperature Sensor (3 pins): DHT11 Humidity and Temperature Sensor (3 pins) from the design created by John De Cristofaro for Adafruit Industries.
  Adafruit DS1307 RTC Breakout: This is a great battery-backed real time clock (RTC) that allows your microcontroller project to keep track of time even if it is reprogrammed, or if the power is lost. Perfect for datalogging, clock-building, time stamping, timers and alarms, etc. The DS1307 is the most popular RTC - but it requires 5V power to work (although we've used it with 5V power and 3.3V logic successfully) PCB &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
  2-Channel 5v Relay Shield: 2 Channel 5v Relay Shield w. 2x SPD-06VDC-SD-C
  Module display OLED I2C 128x64 SSD1306: Ecran OLED I2C SSD163 de 128x64 avec connexion I2C
